// Logisim project alu.circ as structural Verilog: 1 circuit, main circuit alu
module alu (
  input  [31:0] A,
  input  [31:0] B,
  input  [3:0] ALUSel,
  output [31:0] ALUResult
);

  wire [31:0] add0, and7, mul8, mulh9, mulhu11, or6, sll1, slt2, sra13, srl5, sub12, subtractor_1_out, xor4;

  Shifter #(.width(32)) shifter_1 (.in(A), .\dist (B[4:0]), .out(sll1));
  Shifter #(.shift("lr"), .width(32)) shifter_2 (.in(A), .\dist (B[4:0]), .out(srl5));
  Subtractor #(.width(32)) subtractor_1 (.a(A), .b(B), .out(subtractor_1_out));  // open: bin, bout
  Subtractor #(.width(32)) subtractor_2 (.a(A), .b(B), .out(sub12));  // open: bin, bout
  assign or6 = B | A;  // OR_Gate or_1, 32 bits wide
  assign slt2 = {{31{1'b0}}, subtractor_1_out[31]};  // Bit_Extender bit_extender_1
  Multiplexer #(.select(4), .width(32)) multiplexer_1 (
    .in0(add0), .in1(sll1), .in2(slt2), .in4(xor4), .in5(srl5), .in6(or6), .in7(and7), .in8(mul8),
    .in9(mulh9), .in11(mulhu11), .in12(sub12), .in13(sra13), .in15(B), .out(ALUResult), .sel(ALUSel));  // open: in3, in10, in14
  Adder #(.width(32)) adder_1 (.a(A), .b(B), .out(add0));  // open: cin, cout
  Shifter #(.shift("ar"), .width(32)) shifter_3 (.in(A), .\dist (B[4:0]), .out(sra13));
  assign and7 = B & A;  // AND_Gate and_1, 32 bits wide
  assign xor4 = B ^ A;  // XOR_Gate xor_1, 32 bits wide
  Multiplier #(.mode("twosComplement"), .width(32)) multiplier_1 (.a(A), .b(B), .out(mul8), .cout(mulh9));  // open: cin
  Multiplier #(.width(32)) multiplier_2 (.a(A), .b(B), .cout(mulhu11));  // open: out, cin

  // Notes on the sheet:
  //   INPUTS to your circuit
  //   DON'T CHANGE THE LOCATIONS OF THE INPUTS AND OUTPUTS!
  //   OUTPUT from your circuit
endmodule
