// Logisim project branch-comp.circ as structural Verilog: 1 circuit, main circuit branch_comp
module branch_comp (
  input  [31:0] BrData1,
  input  [31:0] BrData2,
  input  BrUn,
  output BrEq,
  output BrLt
);

  wire es, eu, ls, lu;

  Comparator #(.width(32)) comparator_1 (.a(BrData1), .b(BrData2), .eq(es), .lt(ls));  // open: gt
  Comparator #(.mode("unsigned"), .width(32)) comparator_2 (.a(BrData1), .b(BrData2), .eq(eu), .lt(lu));  // open: gt
  Multiplexer multiplexer_1 (.in0(es), .in1(eu), .out(BrEq), .sel(BrUn));
  Multiplexer multiplexer_2 (.in0(ls), .in1(lu), .out(BrLt), .sel(BrUn));

  // Notes on the sheet:
  //   INPUTS to your circuit
  //   DON'T CHANGE THE LOCATIONS OF THE INPUTS AND OUTPUTS!
  //   OUTPUT from your circuit
endmodule
