// Logisim project control-logic.circ as structural Verilog: 1 circuit, main circuit control_logic
module control_logic (
  input  [31:0] Instruction,
  input  BrEq,
  input  BrLt,
  output PCSel,
  output RegWEn,
  output [2:0] ImmSel,
  output BrUn,
  output ASel,
  output BSel,
  output [3:0] ALUSel,
  output MemWEn,
  output [1:0] WBSel
);

  wire addalu, addi, addr, alu1, alu2, alu3, and_11_out, and_12_out, and_13_out, and_14_out, and_15_out,
       and_16_out, and_27_out, andalu, andi, andr, B, B1, B2, comparator_8_eq, comparator_9_eq, f0, f1, f2,
       I1, I2, I3, J, mulalu, mulhalu, mulhr, mulhualu, mulhur, mulr, not_1_out, not_2_out, not_3_out,
       not_4_out, or_1_out, oralu, ori, orr, R, S, sllalu, slli, sllr, sltalu, slti, sltr, sraalu, srai,
       srar, srlalu, srli, srlr, subalu, subr, U1, U2, xoralu, xori, xorr;
  wire [4:0] priority_encoder_1_out;
  wire [5:0] address;
  wire [15:14] rom_1_data;

  Comparator #(.width(7)) comparator_1 (.a(Instruction[6:0]), .b(7'b0110011), .eq(R));  // open: gt, lt
  Comparator #(.width(7)) comparator_2 (.a(Instruction[6:0]), .b(7'b0000011), .eq(I1));  // open: gt, lt
  Comparator #(.width(7)) comparator_3 (.a(Instruction[6:0]), .b(7'b0010011), .eq(I2));  // open: gt, lt
  Comparator #(.width(7)) comparator_4 (.a(Instruction[6:0]), .b(7'b0100011), .eq(S));  // open: gt, lt
  Comparator #(.width(7)) comparator_5 (.a(Instruction[6:0]), .b(7'b0010111), .eq(U1));  // open: gt, lt
  Comparator #(.width(7)) comparator_6 (.a(Instruction[6:0]), .b(7'b0110111), .eq(U2));  // open: gt, lt
  Comparator #(.width(7)) comparator_7 (.a(Instruction[6:0]), .b(7'b1101111), .eq(J));  // open: gt, lt
  Comparator #(.width(7)) comparator_8 (.a(Instruction[6:0]), .b(7'b1100111), .eq(comparator_8_eq));  // open: gt, lt
  Comparator #(.width(3)) comparator_9 (.a(Instruction[14:12]), .b(3'b000), .eq(comparator_9_eq));  // open: gt, lt
  ROM #(.addrWidth(6), .dataWidth(16)) rom_1 (
    .addr(address), .data({rom_1_data, WBSel, MemWEn, ALUSel, BSel, ASel, BrUn, ImmSel, RegWEn}));
  and and_1 (I3, comparator_8_eq, comparator_9_eq);
  not not_1 (not_1_out, Instruction[13]);
  Comparator #(.width(7)) comparator_10 (.a(Instruction[6:0]), .b(7'b1100011), .eq(B));  // open: gt, lt
  and and_2 (B2, B, Instruction[13]);
  and and_3 (B1, B, not_1_out);
  Priority_Encoder #(.select_enc(5)) priority_encoder_1 (
    .in0(addr), .in1(mulr), .in2(subr), .in3(sllr), .in4(mulhr), .in5(mulhur), .in6(sltr), .in7(xorr),
    .in8(srlr), .in9(srar), .in10(orr), .in11(andr), .in12(I1), .in13(addi), .in14(slli), .in15(slti),
    .in16(xori), .in17(srli), .in18(srai), .in19(ori), .in20(andi), .in21(S), .in22(B1), .in23(B2),
    .in24(U1), .in25(U2), .in26(J), .in27(I3), .out(priority_encoder_1_out));  // open: in28, in29, in30, in31, gs, en_out, en_in
  assign address = {{1{1'b0}}, priority_encoder_1_out};  // Bit_Extender bit_extender_1
  Comparator #(.width(3)) comparator_11 (.a(Instruction[14:12]), .b(3'b000), .eq(alu1));  // open: gt, lt
  Comparator #(.width(3)) comparator_12 (.a(Instruction[14:12]), .b(3'b001), .eq(alu2));  // open: gt, lt
  Comparator #(.width(3)) comparator_13 (.a(Instruction[14:12]), .b(3'b001), .eq(mulhualu));  // open: gt, lt
  Comparator #(.width(3)) comparator_14 (.a(Instruction[14:12]), .b(3'b010), .eq(sltalu));  // open: gt, lt
  Comparator #(.width(3)) comparator_15 (.a(Instruction[14:12]), .b(3'b100), .eq(xoralu));  // open: gt, lt
  Comparator #(.width(3)) comparator_16 (.a(Instruction[14:12]), .b(3'b101), .eq(alu3));  // open: gt, lt
  Comparator #(.width(3)) comparator_17 (.a(Instruction[14:12]), .b(3'b110), .eq(oralu));  // open: gt, lt
  Comparator #(.width(3)) comparator_18 (.a(Instruction[14:12]), .b(3'b111), .eq(andalu));  // open: gt, lt
  Comparator #(.width(7)) comparator_19 (.a(Instruction[31:25]), .b({7{1'b0}}), .eq(f0));  // open: gt, lt
  Comparator #(.width(7)) comparator_20 (.a(Instruction[31:25]), .b(7'b0000001), .eq(f1));  // open: gt, lt
  Comparator #(.width(7)) comparator_21 (.a(Instruction[31:25]), .b(7'b0100000), .eq(f2));  // open: gt, lt
  not not_2 (not_2_out, BrLt);
  not not_3 (not_3_out, BrLt);
  and and_4 (addalu, alu1, f0);
  and and_5 (mulalu, alu1, f1);
  and and_6 (subalu, alu1, f2);
  and and_7 (sllalu, alu2, f0);
  and and_8 (mulhalu, alu2, f1);
  and and_9 (srlalu, alu3, f0);
  and and_10 (sraalu, alu3, f2);
  not not_4 (not_4_out, BrEq);
  and and_11 (and_11_out, alu1, BrEq);
  and and_12 (and_12_out, alu3, not_2_out);
  and and_13 (and_13_out, andalu, not_3_out);
  and and_14 (and_14_out, oralu, BrLt);
  and and_15 (and_15_out, xoralu, BrLt);
  and and_16 (and_16_out, mulhualu, not_4_out);
  or or_1 (or_1_out, and_11_out, and_12_out, and_13_out, and_14_out, and_15_out, and_16_out);
  and and_17 (subr, subalu, R);
  and and_18 (sllr, sllalu, R);
  and and_19 (mulhr, mulhalu, R);
  and and_20 (srlr, srlalu, R);
  and and_21 (srar, sraalu, R);
  and and_22 (mulhur, mulhualu, R);
  and and_23 (sltr, sltalu, R);
  and and_24 (xorr, xoralu, R);
  and and_25 (orr, oralu, R);
  and and_26 (andr, andalu, R);
  and and_27 (and_27_out, or_1_out, B);
  and and_28 (addi, alu1, I2);
  and and_29 (slli, sllalu, I2);
  and and_30 (slti, sltalu, I2);
  and and_31 (xori, xoralu, I2);
  and and_32 (srli, srlalu, I2);
  and and_33 (srai, sraalu, I2);
  and and_34 (ori, oralu, I2);
  and and_35 (andi, andalu, I2);
  and and_36 (addr, addalu, R);
  and and_37 (mulr, mulalu, R);
  or or_2 (PCSel, and_27_out, J, I3);

  // Other names for the same wires on the sheet: op[6:0] = Instruction[6:0]; funct3[2:0] = Instruction[14:12];
  //   bit = Instruction[13]; funct7[6:0] = Instruction[31:25]

  // Notes on the sheet:
  //   INPUTS to your circuit
  //   contents of rom_1 (hex, n*v repeats v):
  //   1001 1401 1601 1081 1481 1581 1101 1201 1281 1681 1301 1381 41 1041 10c1 1141 1241 12c1 16c1 1341
  //   13c1 842 64 74 1067 17c7 2069 2041
  //   ROM FOR CONTROL LOGIC
  //   DON'T CHANGE THE LOCATIONS OF THE INPUTS AND OUTPUTS!
  //   This is only if you choose to do the ROM option
  //   OUTPUT from your circuit
  //   Reminder: If using ROM, use combinational logic for PCSel
endmodule
