// Logisim project imm-gen.circ as structural Verilog: 1 circuit, main circuit imm_gen
module imm_gen (
  input  [31:0] Instruction,
  input  [2:0] ImmSel,
  output [31:0] Immediate
);

  wire [31:0] ImmediateB, ImmediateI, ImmediateS;
  wire [31:20] ImmediateJ;

  assign ImmediateJ = {{11{Instruction[31]}}, Instruction[31]};  // Bit_Extender bit_extender_1
  assign ImmediateI = {{20{Instruction[31]}}, Instruction[31:20]};  // Bit_Extender bit_extender_2
  assign ImmediateS = {{20{Instruction[31]}}, {Instruction[31:25], Instruction[11:7]}};  // Bit_Extender bit_extender_3
  assign ImmediateB = {{19{Instruction[31]}}, {Instruction[31], Instruction[7], Instruction[30:25], Instruction[11:8], 1'b0}};  // Bit_Extender bit_extender_4
  Multiplexer #(.select(3), .width(32)) multiplexer_1 (
    .in0(ImmediateI), .in1(ImmediateS), .in2(ImmediateB), .in3({Instruction[31:12], {12{1'b0}}}),
    .in4({ImmediateJ, Instruction[19:12], Instruction[20], Instruction[30:21], 1'b0}), .out(Immediate),
    .sel(ImmSel));  // open: in5, in6, in7

  // Other names for the same wires on the sheet: b1[3:0] = Instruction[11:8]; b3 = Instruction[7];
  //   c3[7:0] = Instruction[19:12]; ImmediateJ[19:1] = {Instruction[19:12], Instruction[20], Instruction[30:21]};
  //   ImmediateU[31:12] = Instruction[31:12]; c2 = Instruction[20]; c1[9:0] = Instruction[30:21];
  //   b2[5:0] = Instruction[30:25]; b4 = Instruction[31]; c4 = Instruction[31]

  // Notes on the sheet:
  //   INPUTS to your circuit
  //   DON'T CHANGE THE LOCATIONS OF THE INPUTS AND OUTPUTS!
  //   OUTPUT from your circuit
endmodule
