// Logisim project partial-load.circ as structural Verilog: 1 circuit, main circuit partial_load
module partial_load (
  input  [31:0] Instruction,
  input  [31:0] MemAddress,
  input  [31:0] DataFromMem,
  output [31:0] DataToReg
);

  wire I;
  wire [7:0] multiplexer_1_out;
  wire [15:0] multiplexer_2_out;
  wire [31:0] bit_extender_1_out, bit_extender_2_out, multiplexer_3_out;

  Comparator #(.width(7)) comparator_1 (.a(Instruction[6:0]), .b(7'b0000011), .eq(I));  // open: gt, lt
  Multiplexer #(.select(2), .width(8)) multiplexer_1 (
    .in0(DataFromMem[7:0]), .in1(DataFromMem[15:8]), .in2(DataFromMem[23:16]), .in3(DataFromMem[31:24]),
    .out(multiplexer_1_out), .sel(MemAddress[1:0]));
  Multiplexer #(.select(2), .width(16)) multiplexer_2 (
    .in0(DataFromMem[15:0]), .in1(DataFromMem[23:8]), .in2(DataFromMem[31:16]), .out(multiplexer_2_out),
    .sel(MemAddress[1:0]));  // open: in3
  assign bit_extender_1_out = {{24{multiplexer_1_out[7]}}, multiplexer_1_out};  // Bit_Extender bit_extender_1
  assign bit_extender_2_out = {{16{multiplexer_2_out[15]}}, multiplexer_2_out};  // Bit_Extender bit_extender_2
  Multiplexer #(.select(3), .width(32)) multiplexer_3 (
    .in0(bit_extender_1_out), .in1(bit_extender_2_out), .in2(DataFromMem), .out(multiplexer_3_out),
    .sel(Instruction[14:12]));  // open: in3, in4, in5, in6, in7
  assign DataToReg = I ? multiplexer_3_out : 32'bz;  // Controlled_Buffer controlled_buffer_1

  // Other names for the same wires on the sheet: m[15:0] = DataFromMem[23:8]; op[6:0] = Instruction[6:0];
  //   funct3[2:0] = Instruction[14:12]

  // Notes on the sheet:
  //   INPUTS to your circuit
  //   DON'T CHANGE THE LOCATIONS OF THE INPUTS AND OUTPUTS!
  //   OUTPUT from your circuit
endmodule
