// Logisim project partial-store.circ as structural Verilog: 1 circuit, main circuit partial_store
module partial_store (
  input  [31:0] Instruction,
  input  [31:0] MemAddress,
  input  [31:0] DataFromReg,
  input  MemWEn,
  output [3:0] MemWriteMask,
  output [31:0] DataToMem
);

  wire [3:0] decoder_1_out0, multiplexer_5_out;
  wire [3:1] decoder_2_out0;
  wire [15:0] bit_extender_3_out;
  wire [23:0] bit_extender_2_out;
  wire [31:0] bit_extender_1_out, bit_extender_4_out, multiplexer_1_out, multiplexer_2_out, multiplexer_3_out;

  assign bit_extender_1_out = {{24{1'b0}}, DataFromReg[7:0]};  // Bit_Extender bit_extender_1
  assign bit_extender_2_out = {{16{1'b0}}, DataFromReg[7:0]};  // Bit_Extender bit_extender_2
  assign bit_extender_3_out = {{8{1'b0}}, DataFromReg[7:0]};  // Bit_Extender bit_extender_3
  assign bit_extender_4_out = {{16{1'b0}}, DataFromReg[15:0]};  // Bit_Extender bit_extender_4
  Multiplexer #(.select(2), .width(32)) multiplexer_1 (
    .in0(bit_extender_4_out), .in2({DataFromReg[15:0], {16{1'b0}}}), .out(multiplexer_1_out),
    .sel(MemAddress[1:0]));  // open: in1, in3
  Multiplexer #(.select(2), .width(32)) multiplexer_2 (
    .in0(bit_extender_1_out), .in1({bit_extender_2_out, {8{1'b0}}}), .in2({bit_extender_3_out, {16{1'b0}}}),
    .in3({DataFromReg[7:0], {24{1'b0}}}), .out(multiplexer_2_out), .sel(MemAddress[1:0]));
  Multiplexer #(.select(3), .width(32)) multiplexer_3 (
    .in0(multiplexer_2_out), .in1(multiplexer_1_out), .in2(DataFromReg), .out(multiplexer_3_out),
    .sel(Instruction[14:12]));  // open: in3, in4, in5, in6, in7
  Decoder #(.enable("false"), .select(2)) decoder_1 (
    .out0(decoder_1_out0[0]), .out1(decoder_1_out0[1]), .out2(decoder_1_out0[2]), .out3(decoder_1_out0[3]),
    .sel(MemAddress[1:0]));
  Decoder #(.enable("false"), .select(2)) decoder_2 (
    .out0(decoder_2_out0[1]), .out2(decoder_2_out0[3]), .sel(MemAddress[1:0]));  // open: out1, out3
  Multiplexer #(.width(32)) multiplexer_4 (.in0({32{1'b0}}), .in1(multiplexer_3_out), .out(DataToMem), .sel(MemWEn));
  Multiplexer #(.select(3), .width(4)) multiplexer_5 (
    .in0(decoder_1_out0), .in1({{2{decoder_2_out0[3]}}, {2{decoder_2_out0[1]}}}), .in2(4'b1111),
    .out(multiplexer_5_out), .sel(Instruction[14:12]));  // open: in3, in4, in5, in6, in7
  Multiplexer #(.width(4)) multiplexer_6 (.in0(4'b0000), .in1(multiplexer_5_out), .out(MemWriteMask), .sel(MemWEn));

  // Other names for the same wires on the sheet: m[1:0] = MemAddress[1:0]

  // Notes on the sheet:
  //   INPUTS to your circuit
  //   DON'T CHANGE THE LOCATIONS OF THE INPUTS AND OUTPUTS!
  //   OUTPUT from your circuit
endmodule
