// Logisim project regfile.circ as structural Verilog: 1 circuit, main circuit regfile
module regfile (
  input  [4:0] ReadIndex1,
  input  [4:0] ReadIndex2,
  input  [4:0] WriteIndex,
  input  [31:0] WriteData,
  input  RegWEn,
  input  clk,
  output [31:0] ra,
  output [31:0] sp,
  output [31:0] t0,
  output [31:0] t1,
  output [31:0] t2,
  output [31:0] s0,
  output [31:0] s1,
  output [31:0] a0,
  output [31:0] ReadData1,
  output [31:0] ReadData2
);

  wire WE1, WE2, WE3, WE4, WE5, WE6, WE7, WE8, WE9, WE10, WE11, WE12, WE13, WE14, WE15, WE16, WE17, WE18,
       WE19, WE20, WE21, WE22, WE23, WE24, WE25, WE26, WE27, WE28, WE29, WE30, WE31;
  wire [31:0] o3, o4, o11, o12, o13, o14, o15, o16, o17, o18, o19, o20, o21, o22, o23, o24, o25, o26, o27,
       o28, o29, o30, o31;

  Decoder #(.select(5)) decoder_1 (
    .out1(WE1), .out2(WE2), .out3(WE3), .out4(WE4), .out5(WE5), .out6(WE6), .out7(WE7), .out8(WE8),
    .out9(WE9), .out10(WE10), .out11(WE11), .out12(WE12), .out13(WE13), .out14(WE14), .out15(WE15),
    .out16(WE16), .out17(WE17), .out18(WE18), .out19(WE19), .out20(WE20), .out21(WE21), .out22(WE22),
    .out23(WE23), .out24(WE24), .out25(WE25), .out26(WE26), .out27(WE27), .out28(WE28), .out29(WE29),
    .out30(WE30), .out31(WE31), .sel(WriteIndex), .en(RegWEn));  // open: out0
  Register #(.width(32)) x3 (.D(WriteData), .en(WE3), .clk(clk), .Q(o3));  // open: clr
  Register #(.width(32)) x6 (.D(WriteData), .en(WE6), .clk(clk), .Q(t1));  // open: clr
  Register #(.width(32)) x9 (.D(WriteData), .en(WE9), .clk(clk), .Q(s1));  // open: clr
  Register #(.width(32)) register_1 (.D(WriteData), .en(WE12), .clk(clk), .Q(o12));  // open: clr
  Register #(.width(32)) register_2 (.D(WriteData), .en(WE15), .clk(clk), .Q(o15));  // open: clr
  Register #(.width(32)) register_3 (.D(WriteData), .en(WE18), .clk(clk), .Q(o18));  // open: clr
  Register #(.width(32)) register_4 (.D(WriteData), .en(WE21), .clk(clk), .Q(o21));  // open: clr
  Register #(.width(32)) register_5 (.D(WriteData), .en(WE24), .clk(clk), .Q(o24));  // open: clr
  Register #(.width(32)) register_6 (.D(WriteData), .en(WE27), .clk(clk), .Q(o27));  // open: clr
  Register #(.width(32)) register_7 (.D(WriteData), .en(WE30), .clk(clk), .Q(o30));  // open: clr
  Multiplexer #(.select(5), .width(32)) multiplexer_1 (
    .in0({32{1'b0}}), .in1(ra), .in2(sp), .in3(o3), .in4(o4), .in5(t0), .in6(t1), .in7(t2), .in8(s0),
    .in9(s1), .in10(a0), .in11(o11), .in12(o12), .in13(o13), .in14(o14), .in15(o15), .in16(o16), .in17(o17),
    .in18(o18), .in19(o19), .in20(o20), .in21(o21), .in22(o22), .in23(o23), .in24(o24), .in25(o25),
    .in26(o26), .in27(o27), .in28(o28), .in29(o29), .in30(o30), .in31(o31), .out(ReadData1), .sel(ReadIndex1));
  Multiplexer #(.select(5), .width(32)) multiplexer_2 (
    .in0({32{1'b0}}), .in1(ra), .in2(sp), .in3(o3), .in4(o4), .in5(t0), .in6(t1), .in7(t2), .in8(s0),
    .in9(s1), .in10(a0), .in11(o11), .in12(o12), .in13(o13), .in14(o14), .in15(o15), .in16(o16), .in17(o17),
    .in18(o18), .in19(o19), .in20(o20), .in21(o21), .in22(o22), .in23(o23), .in24(o24), .in25(o25),
    .in26(o26), .in27(o27), .in28(o28), .in29(o29), .in30(o30), .in31(o31), .out(ReadData2), .sel(ReadIndex2));
  Register #(.width(32)) x1 (.D(WriteData), .en(WE1), .clk(clk), .Q(ra));  // open: clr
  Register #(.width(32)) x4 (.D(WriteData), .en(WE4), .clk(clk), .Q(o4));  // open: clr
  Register #(.width(32)) x7 (.D(WriteData), .en(WE7), .clk(clk), .Q(t2));  // open: clr
  Register #(.width(32)) x10 (.D(WriteData), .en(WE10), .clk(clk), .Q(a0));  // open: clr
  Register #(.width(32)) register_8 (.D(WriteData), .en(WE13), .clk(clk), .Q(o13));  // open: clr
  Register #(.width(32)) register_9 (.D(WriteData), .en(WE16), .clk(clk), .Q(o16));  // open: clr
  Register #(.width(32)) register_10 (.D(WriteData), .en(WE19), .clk(clk), .Q(o19));  // open: clr
  Register #(.width(32)) register_11 (.D(WriteData), .en(WE22), .clk(clk), .Q(o22));  // open: clr
  Register #(.width(32)) register_12 (.D(WriteData), .en(WE25), .clk(clk), .Q(o25));  // open: clr
  Register #(.width(32)) register_13 (.D(WriteData), .en(WE28), .clk(clk), .Q(o28));  // open: clr
  Register #(.width(32)) register_14 (.D(WriteData), .en(WE31), .clk(clk), .Q(o31));  // open: clr
  Register #(.width(32)) x2 (.D(WriteData), .en(WE2), .clk(clk), .Q(sp));  // open: clr
  Register #(.width(32)) x5 (.D(WriteData), .en(WE5), .clk(clk), .Q(t0));  // open: clr
  Register #(.width(32)) x8 (.D(WriteData), .en(WE8), .clk(clk), .Q(s0));  // open: clr
  Register #(.width(32)) register_15 (.D(WriteData), .en(WE11), .clk(clk), .Q(o11));  // open: clr
  Register #(.width(32)) register_16 (.D(WriteData), .en(WE14), .clk(clk), .Q(o14));  // open: clr
  Register #(.width(32)) register_17 (.D(WriteData), .en(WE17), .clk(clk), .Q(o17));  // open: clr
  Register #(.width(32)) register_18 (.D(WriteData), .en(WE20), .clk(clk), .Q(o20));  // open: clr
  Register #(.width(32)) register_19 (.D(WriteData), .en(WE23), .clk(clk), .Q(o23));  // open: clr
  Register #(.width(32)) register_20 (.D(WriteData), .en(WE26), .clk(clk), .Q(o26));  // open: clr
  Register #(.width(32)) register_21 (.D(WriteData), .en(WE29), .clk(clk), .Q(o29));  // open: clr

  // Other names for the same wires on the sheet: o1[31:0] = ra; o2[31:0] = sp; o5[31:0] = t0; o6[31:0] = t1;
  //   o7[31:0] = t2; o8[31:0] = s0; o9[31:0] = s1; o10[31:0] = a0

  // Notes on the sheet:
  //   INPUTS to your circuit
  //   DON'T CHANGE THE LOCATIONS OF THE INPUTS AND OUTPUTS!
  //   These are DEBUG/TEST outputs from your circuit.
  //   OUTPUTS from your circuit
endmodule
